// Logisim project HW4.circ as structural Verilog: 10 circuits, main circuit main
module main (
);

  wire clock_1_out;
  wire [15:0] adder_1_out, ram_1_dout, register_1_q;

  Clock clock_1 (.out(clock_1_out));
  Register #(.width(16)) register_1 (.D(adder_1_out), .en(1'b1), .Q(register_1_q), .clk(clock_1_out));  // open: clr
  Adder #(.width(16)) adder_1 (.a(16'h1), .b(register_1_q), .out(adder_1_out));  // open: cin, cout
  RAM #(.addrWidth(16), .dataWidth(16)) ram_1 (
    .addr(register_1_q), .clk(clock_1_out), .dout(ram_1_dout));  // open: we, oe, din
  Register #(.width(16)) register_2 (.D(ram_1_dout), .clk(clock_1_out));  // open: en, Q, clr
endmodule

module ALU (
  input  [15:0] A,
  input  [15:0] B,
  input  [1:0] ALU_Control,
  output [15:0] ALU_out
);

  wire [15:0] adder_1_out, and_1_out, or_1_out, subtractor_1_out;

  Adder #(.width(16)) adder_1 (.a(A), .b(B), .out(adder_1_out));  // open: cin, cout
  Subtractor #(.width(16)) subtractor_1 (.a(A), .b(B), .out(subtractor_1_out));  // open: bin, bout
  assign and_1_out = A & B;  // AND_Gate and_1, 16 bits wide
  assign or_1_out = A | B;  // OR_Gate or_1, 16 bits wide
  Multiplexer #(.select(2), .width(16)) multiplexer_1 (
    .in0(adder_1_out), .in1(and_1_out), .in2(or_1_out), .in3(subtractor_1_out), .out(ALU_out),
    .sel(ALU_Control), .en(1'b1));
endmodule

module CU (
  input  [3:0] in_1,
  output out_2,
  output out_3,
  output out_4,
  output out_5,
  output out_6,
  output out_7,
  output out_8
);

  RegDst regdst_1 (.OpCode(in_1), .Reg_Dst(out_2));
  ALUSrc alusrc_1 (.OpCode(in_1), .ALU_Src(out_3));
  MemToReg memtoreg_1 (.OpCode(in_1), .Mem_ToReg(out_4));
  RegWrite regwrite_1 (.OpCode(in_1), .Reg_Write(out_5));
  MemRead memread_1 (.OpCode(in_1), .Mem_Read(out_6));
  MemWrite memwrite_1 (.OpCode(in_1), .Mem_Write(out_7));
  Branch branch_1 (.OpCode(in_1), .Branch_Out(out_8));
endmodule

module RegDst (
  input  [3:0] OpCode,
  output Reg_Dst
);

  wire A_NOT_C_out, and_1_out, and_2_out, and_3_out, and_4_out, not_1_out, not_2_out, not_3_out, or_1_out;

  not not_1 (not_1_out, OpCode[1]);
  not not_2 (not_2_out, OpCode[3]);
  and A_NOT_C (A_NOT_C_out, OpCode[3], not_1_out);
  and and_1 (and_1_out, not_2_out, OpCode[2]);
  and and_2 (and_2_out, OpCode[2], OpCode[1]);
  not not_3 (not_3_out, OpCode[0]);
  and and_3 (and_3_out, and_1_out, OpCode[1]);
  and and_4 (and_4_out, and_2_out, not_3_out);
  or or_1 (or_1_out, A_NOT_C_out, and_3_out);
  or or_2 (Reg_Dst, or_1_out, and_4_out);
endmodule

module ALUSrc (
  input  [3:0] OpCode,
  output ALU_Src
);

  wire and_1_out, and_2_out, and_3_out, and_4_out, and_5_out, and_6_out, not_1_out, not_2_out, not_3_out,
       or_1_out;

  not not_1 (not_1_out, OpCode[3]);
  and and_1 (and_1_out, not_1_out, OpCode[2]);
  and and_2 (and_2_out, OpCode[3], not_2_out);
  not not_2 (not_2_out, OpCode[2]);
  and and_3 (and_3_out, OpCode[3], OpCode[1]);
  and and_4 (and_4_out, and_1_out, OpCode[1]);
  and and_5 (and_5_out, and_2_out, not_3_out);
  not not_3 (not_3_out, OpCode[0]);
  and and_6 (and_6_out, and_3_out, OpCode[0]);
  or or_1 (or_1_out, and_4_out, and_5_out);
  or or_2 (ALU_Src, or_1_out, and_6_out);
endmodule

module MemToReg (
  input  [3:0] OpCode,
  output Mem_ToReg
);

  wire and_1_out;

  and and_1 (and_1_out, OpCode[3], OpCode[1]);
  and and_2 (Mem_ToReg, and_1_out, OpCode[0]);
endmodule

module RegWrite (
  input  [3:0] OpCode,
  output Reg_Write
);

  wire and_1_out, and_2_out, and_3_out, not_1_out, or_1_out;

  and and_1 (and_1_out, OpCode[2], OpCode[1]);
  and and_2 (and_2_out, OpCode[3], not_1_out);
  not not_1 (not_1_out, OpCode[1]);
  and and_3 (and_3_out, OpCode[3], OpCode[0]);
  or or_1 (or_1_out, and_1_out, and_2_out);
  or or_2 (Reg_Write, or_1_out, and_3_out);
endmodule

module MemRead (
  input  [3:0] OpCode,
  output Mem_Read
);

  wire and_1_out, and_2_out, not_1_out;

  not not_1 (not_1_out, OpCode[2]);
  and and_1 (and_1_out, OpCode[3], not_1_out);
  and and_2 (and_2_out, OpCode[1], OpCode[0]);
  and and_3 (Mem_Read, and_1_out, and_2_out);
endmodule

module MemWrite (
  input  [3:0] OpCode,
  output Mem_Write
);

  wire and_1_out, and_2_out, not_1_out, not_2_out;

  not not_1 (not_1_out, OpCode[2]);
  not not_2 (not_2_out, OpCode[0]);
  and and_1 (and_1_out, OpCode[3], not_1_out);
  and and_2 (and_2_out, OpCode[1], not_2_out);
  and and_3 (Mem_Write, and_1_out, and_2_out);
endmodule

module Branch (
  input  [3:0] OpCode,
  output Branch_Out
);

  wire and_1_out, not_1_out, not_2_out;

  not not_1 (not_1_out, OpCode[3]);
  and and_1 (and_1_out, not_1_out, OpCode[2]);
  not not_2 (not_2_out, OpCode[1]);
  and and_2 (Branch_Out, and_1_out, not_2_out);
endmodule
